# Fritzing sketch schematic (saved by Fritzing 0.9.10b)
breadboards: 1

parts:
  Teensy1 = Teensy 4.0
  R1 = Resistor [tolerance=±5% power=0.25 resistance=220 package=THT]
  R2 = Resistor [tolerance=±5% power=0.25 resistance=220 package=THT]
  R3 = Resistor [tolerance=±5% power=0.25 resistance=220 package=THT]
  S1 = Pushbutton [package="[THT]"]
  R4 = Resistor [tolerance=±5% power=0.25 resistance=220 package=THT]
  S2 = Pushbutton [package="[THT]"]
  LED1 = RGB LED (com. cathode, rgb) [package="5 mm [THT]"]

nets:
  N1: Teensy1.pin_1, Teensy1.pin_6, Teensy1.pin_32, R1.Pin_1, R2.Pin_1, R3.Pin_1, S1.Pin_3, S1.Pin_4, S2.Pin_1, S2.Pin_2, LED1.common_cathode
  N2: Teensy1.pin_4, R3.Pin_0, LED1.blue_anode
  N3: Teensy1.pin_5, R1.Pin_0, LED1.green_anode
  N4: Teensy1.pin_7, R2.Pin_0, LED1.red_anode
  N5: Teensy1.pin_25, S1.Pin_1, S1.Pin_2, R4.Pin_1
  N6: Teensy1.pin_26, S2.Pin_3, S2.Pin_4
  N7: Teensy1.pin_31, R4.Pin_0

notes:
  CST8227
  Interfacing Lab 04
  Control a tri-color RGB with two switches and a pullup resistor
  @author Neil Kingdom 040967309

custom parts:
  Teensy 4.0: The Teensy is a complete USB-based microcontoller development system, in a very small footprint, capable of implementing many types of projects. All programming is done via the USB port. No special programmer is needed, only a standard micro-USB cable and a PC or Macintosh with a USB port.
